// Digital circuit Assembler.dig as structural Verilog
module Assembler (
  input  mode,
  input  [15:0] value,
  input  [1:0] dest,
  input  [1:0] src,
  input  add,
  input  jump,
  input  tworeg,
  input  move,
  input  load,
  input  store,
  input  [3:0] address,
  input  [1:0] logic_instr,
  input  logic_en,
  input  sub,
  input  beq,
  output [31:0] inst,
  output store_clk
);

  wire priorityencoder_1_any;

  PriorityEncoder #(.Selector_Bits(3)) priorityencoder_1 (
    .in0(add), .in1(beq), .in2(sub), .in3(logic_en), .in4(store), .in5(load), .in6(move), .in7(jump),
    .num(inst[26:24]), .any(priorityencoder_1_any));
  and and_1 (store_clk, priorityencoder_1_any, mode);

  assign {inst[31:27], inst[23:0]} = {address, tworeg, logic_instr, src, 2'b00, dest, value};
endmodule
