// Digital circuit Decoder.dig as structural Verilog
module Decoder (
  input  [31:0] instr,
  input  [15:0] RR,
  input  [15:0] RL,
  output [1:0] rs,
  output [1:0] rd,
  output add,
  output [15:0] L,
  output [15:0] R,
  output jump,
  output move,
  output [1:0] result_mux,
  output load,
  output store,
  output [3:0] address,
  output [1:0] logic_instr,
  output sub,
  output beq,
  output tworeg,
  output [4:0] op
);

  wire or_2_out;
  wire [1:0] or_1_out;

  Multiplexer #(.Bits(16)) multiplexer_1 (.sel(instr[27]), .in_0(instr[15:0]), .in_1(RR), .out(R));
  Multiplexer #(.Bits(16)) multiplexer_2 (.sel(instr[27]), .in_0(RR), .in_1(RL), .out(L));
  Decoder #(.Selector_Bits(3)) decoder_1 (
    .sel(instr[26:24]), .out_0(add), .out_1(beq), .out_2(sub), .out_4(store), .out_5(load), .out_6(move),
    .out_7(jump));  // open: out_3
  Multiplexer #(.Bits(5)) multiplexer_3 (
    .sel(or_2_out), .in_0({2'b00, instr[26:24]}), .in_1({instr[23:22], 3'b001}), .out(op));
  assign or_1_out = instr[23:22] | 2'b00;  // Or or_1, 2 bits wide
  or or_2 (or_2_out, or_1_out[0], or_1_out[1]);
  PriorityEncoder #(.Selector_Bits(2)) priorityencoder_1 (
    .in0(jump), .in1(add), .in2(move), .in3(beq), .num(result_mux));  // open: any

  assign address = instr[31:28];
  assign logic_instr = instr[23:22];
  assign rd = instr[17:16];
  assign rs = instr[21:20];
  assign tworeg = instr[27];
endmodule
