// Digital circuit Execute.dig as structural Verilog
module Execute (
  input  [15:0] L,
  input  [15:0] R,
  input  [1:0] result_mux,
  input  [1:0] logic_instr,
  input  sub,
  input  beq,
  output [15:0] O,
  output Flag_zero,
  output Flag_OVR
);

  wire comparator_1_eq;
  wire [15:0] add_1_s, and_1_out, multiplexer_1_out, multiplexer_3_out, or_1_out, sub_1_s, xor_1_out;

  assign xor_1_out = R ^ L;  // XOr xor_1, 16 bits wide
  assign and_1_out = R & L;  // And and_1, 16 bits wide
  assign or_1_out = R | L;  // Or or_1, 16 bits wide
  Add #(.Bits(16)) add_1 (.a(L), .b(R), .c_i(1'b0), .s(add_1_s));  // open: c_o
  Sub #(.Bits(16)) sub_1 (.a(L), .b(R), .c_i(1'b0), .s(sub_1_s), .c_o(Flag_OVR));
  Comparator #(.Bits(16)) comparator_1 (.a(sub_1_s), .b({16{1'b0}}), .eq(comparator_1_eq));  // open: gt, lt
  Multiplexer #(.Selector_Bits(2), .Bits(16)) multiplexer_1 (
    .sel(result_mux), .in_0(L), .in_1(R), .in_2(add_1_s), .in_3(L), .out(multiplexer_1_out));
  Multiplexer multiplexer_2 (.sel(beq), .in_0(1'b0), .in_1(comparator_1_eq), .out(Flag_zero));
  Multiplexer #(.Bits(16)) multiplexer_3 (.sel(sub), .in_0(multiplexer_1_out), .in_1(sub_1_s), .out(multiplexer_3_out));
  Multiplexer #(.Selector_Bits(2), .Bits(16)) multiplexer_4 (
    .sel(logic_instr), .in_0(multiplexer_3_out), .in_1(and_1_out), .in_2(or_1_out), .in_3(xor_1_out), .out(O));
endmodule
