// Digital circuit Fetch.dig as structural Verilog
module Fetch (
  input  clock,
  input  [15:0] value,
  input  jump,
  input  prog,
  input  [31:0] bypass,
  input  [31:0] instruction,
  input  Flag_zero,
  input  [3:0] beq_address,
  output [3:0] PC,
  output [31:0] instr_o
);

  wire or_1_out;
  wire [3:0] multiplexer_1_out;

  Multiplexer #(.Bits(4)) multiplexer_1 (
    .sel(Flag_zero), .in_0(value[3:0]), .in_1(beq_address), .out(multiplexer_1_out));
  Multiplexer #(.Bits(32)) multiplexer_2 (.sel(prog), .in_0(instruction), .in_1(bypass), .out(instr_o));
  or or_1 (or_1_out, jump, Flag_zero);
  CounterPreset #(.Bits(4), .isProgramCounter("true")) u_PC (
    .en(1'b1), .C(clock), .dir(1'b0), .in(multiplexer_1_out), .ld(or_1_out), .clr(1'b0), .out(PC));  // open: ovf
endmodule
