// Digital circuit Memory.dig as structural Verilog
module Memory (
  input  clock,
  input  load,
  input  store,
  input  [3:0] address,
  input  [15:0] data_in,
  input  write,
  output [15:0] load_data
);

  wire multiplexer_1_out, or_1_out;

  or or_1 (or_1_out, clock, load, store);
  Multiplexer multiplexer_1 (.sel(write), .in_0(1'b1), .in_1(1'b0), .out(multiplexer_1_out));
  EEPROMDualPort #(.AddrBits(4), .Bits(16)) Memory (
    .A(address), .Din(data_in), .str(write), .C(or_1_out), .ld(multiplexer_1_out), .D(load_data));

  // Notes on the sheet:
  //   contents of Memory (hex, n*v repeats v):
  //   5,2,63,8210000,e130000,d7,9*0,618
endmodule
