// Digital circuit main.dig as structural Verilog
module main (
  input  [15:0] value,
  input  [1:0] dest,
  input  [1:0] src,
  input  tworeg,
  input  [3:0] address,
  input  [1:0] logic_instr,
  input  clock,
  output [15:0] R0,
  output [15:0] R1,
  output [15:0] R2,
  output [15:0] R3,
  output [3:0] PC,
  output [3:0] out_11
);

  wire add, add_out, assembler_1_store_clk, beq, beq_out, decoder_1_sub, Flag_OVR, Flag_zero,
       instrdisplay_1_p1, instrdisplay_1_p2, instrdisplay_1_p3, instrdisplay_1_p4, instrdisplay_1_p5,
       instrdisplay_1_p6, jump, jump_out, load, load_out, logic_en_out, mode_out, move, move_out,
       pcdisplay_1_p1, pcdisplay_1_p2, pcnumdisp_1_p3, regdisplay_1_p1, regdisplay_1_p2, regdisplay_2_p1,
       regdisplay_2_p2, store, store_out, sub_out, tworeg_t;
  wire [1:0] decoder_1_logic_instr, decoder_1_result_mux, rd, rs;
  wire [3:0] pcnumdisp_1_p1;
  wire [4:0] op;
  wire [15:0] decoder_1_l, execute_1_o, instrdisplay_1_d1, instrdisplay_1_d2, instrdisplay_1_d3,
       instrdisplay_1_d4, instrdisplay_1_d5, instrdisplay_1_d6, memory_1_load_data, pcdisplay_1_d1,
       pcdisplay_1_d2, regdisplay_1_d1, regdisplay_1_d2, regdisplay_2_d1, regdisplay_2_d2, regfile_1_rl,
       regfile_1_rr, value_t;
  wire [31:0] assembler_1_inst, fetch_1_instr_o, Program_d;

  DipSwitch mode (.out(mode_out));
  Button u_add (.out(add_out));
  Button u_jump (.out(jump_out));
  Button u_move (.out(move_out));
  Button sub (.out(sub_out));
  Button u_load (.out(load_out));
  Button u_store (.out(store_out));
  Button logic_en (.out(logic_en_out));
  Button u_beq (.out(beq_out));
  LED programming (.in(mode_out));
  Assembler assembler_1 (
    .mode(mode_out), .value(value), .dest(dest), .src(src), .add(add_out), .jump(jump_out), .tworeg(tworeg),
    .move(move_out), .load(load_out), .store(store_out), .address(address), .logic_instr(logic_instr),
    .logic_en(logic_en_out), .sub(sub_out), .beq(beq_out), .inst(assembler_1_inst),
    .store_clk(assembler_1_store_clk));
  SixteenSeg sixteenseg_1 (.led(pcdisplay_1_d1), .dp(pcdisplay_1_p1));
  SixteenSeg sixteenseg_2 (.led(pcdisplay_1_d2), .dp(pcdisplay_1_p2));
  pcdisplay pcdisplay_1 (.D1(pcdisplay_1_d1), .P1(pcdisplay_1_p1), .D2(pcdisplay_1_d2), .P2(pcdisplay_1_p2));
  EEPROMDualPort #(.AddrBits(4), .isProgramMemory("true"), .Bits(32)) Program (
    .A(PC), .Din(assembler_1_inst), .str(1'b1), .C(assembler_1_store_clk), .ld(1'b1), .D(Program_d));
  Seven_Seg_Hex seven_seg_hex_1 (.d(pcnumdisp_1_p1), .dp(pcnumdisp_1_p3));
  // pcnumdisp pcnumdisp_1: pin names not known; wires that end beside it: pcnumdisp_1_p1, PC, pcnumdisp_1_p3
  Fetch fetch_1 (
    .clock(clock), .value(value_t), .jump(jump), .prog(mode_out), .bypass(assembler_1_inst),
    .instruction(Program_d), .Flag_zero(Flag_zero), .beq_address(out_11), .PC(PC), .instr_o(fetch_1_instr_o));
  SixteenSeg sixteenseg_3 (.led(instrdisplay_1_d1), .dp(instrdisplay_1_p1));
  SixteenSeg sixteenseg_4 (.led(instrdisplay_1_d2), .dp(instrdisplay_1_p2));
  SixteenSeg sixteenseg_5 (.led(instrdisplay_1_d3), .dp(instrdisplay_1_p3));
  instrdisplay instrdisplay_1 (
    .D1(instrdisplay_1_d1), .P1(instrdisplay_1_p1), .D2(instrdisplay_1_d2), .P2(instrdisplay_1_p2),
    .D3(instrdisplay_1_d3), .P3(instrdisplay_1_p3), .D4(instrdisplay_1_d4), .P4(instrdisplay_1_p4),
    .D5(instrdisplay_1_d5), .P5(instrdisplay_1_p5), .D6(instrdisplay_1_d6), .P6(instrdisplay_1_p6), .I(op));
  SixteenSeg sixteenseg_6 (.led(instrdisplay_1_d4), .dp(instrdisplay_1_p4));
  SixteenSeg sixteenseg_7 (.led(instrdisplay_1_d5), .dp(instrdisplay_1_p5));
  Decoder decoder_1 (
    .instr(fetch_1_instr_o), .RR(regfile_1_rr), .RL(regfile_1_rl), .rs(rs), .rd(rd), .add(add),
    .L(decoder_1_l), .R(value_t), .jump(jump), .move(move), .result_mux(decoder_1_result_mux), .load(load),
    .store(store), .address(out_11), .logic_instr(decoder_1_logic_instr), .sub(decoder_1_sub), .beq(beq),
    .tworeg(tworeg_t), .op(op));
  SixteenSeg sixteenseg_8 (.led(instrdisplay_1_d6), .dp(instrdisplay_1_p6));
  SixteenSeg sixteenseg_9 (.led(regdisplay_1_d1), .dp(regdisplay_1_p1));
  SixteenSeg sixteenseg_10 (.led(regdisplay_1_d2), .dp(regdisplay_1_p2));
  regdisplay regdisplay_1 (
    .D1(regdisplay_1_d1), .P1(regdisplay_1_p1), .D2(regdisplay_1_d2), .P2(regdisplay_1_p2), .E(1'b1),
    .J(jump), .R(rd));
  SixteenSeg sixteenseg_11 (.led(regdisplay_2_d1), .dp(regdisplay_2_p1));
  SixteenSeg sixteenseg_12 (.led(regdisplay_2_d2), .dp(regdisplay_2_p2));
  regdisplay regdisplay_2 (
    .D1(regdisplay_2_d1), .P1(regdisplay_2_p1), .D2(regdisplay_2_d2), .P2(regdisplay_2_p2), .E(tworeg_t),
    .J(jump), .R(rs));
  LED led_1 (.in(Flag_OVR));
  LED led_2 (.in(Flag_zero));
  Execute execute_1 (
    .L(decoder_1_l), .R(value_t), .result_mux(decoder_1_result_mux), .logic_instr(decoder_1_logic_instr),
    .sub(decoder_1_sub), .beq(beq), .O(execute_1_o), .Flag_zero(Flag_zero), .Flag_OVR(Flag_OVR));
  Memory memory_1 (
    .clock(clock), .load(load), .store(store), .address(out_11), .data_in(value_t), .write(store),
    .load_data(memory_1_load_data));
  RegFile regfile_1 (
    .rs(rs), .clock(clock), .rd(rd), .result(execute_1_o), .load(load), .load_data(memory_1_load_data),
    .R0(R0), .R1(R1), .R2(R2), .R3(R3), .RR(regfile_1_rr), .RL(regfile_1_rl));

  // Other names for the same wires on the sheet: address_t[3:0] = out_11

  // Notes on the sheet:
  //   clock: Hz: 2
  //   contents of Program (hex, n*v repeats v):
  //   601000a,6030000,6020001,99310000,a210000,7000003,6000000,e220000
  //   ,700000f,700000f
endmodule
