// Digital circuit pcnumdisplay.dig as structural Verilog
module pcnumdisplay (
  input  [3:0] PC,
  output [3:0] D1,
  output [3:0] P1
);

  assign D1 = 1'b1 ? PC : 4'bz;  // Driver driver_1
  // Pins of 1 and 4 bits meet at {P1[3:1], 1'b0}

  assign P1[0] = 1'b0;
endmodule
